# Fritzing sketch tuer_beobachter (saved by Fritzing 1.0.5)

parts:
  LCM1602_IIC1 = LCM1602 IIC [part_number="LCM1602 IIC" chip_label="LCM1602 IIC" package="DIP (Dual Inline) [THT]"]
  LCD1 = LCD screen
  Mod1 = Amica NodeMCU DEVKIT 1.0
  J1 = Power Jack [package=power_jack_pth_lock]
  Q1 = PNP-Transistor [package="TO92 [THT]"]
  R1 = Resistor [tolerance=±5% power=0.25W resistance=220 package=THT]
  D2 = Rectifier Diode [part_number=1N4001 package="300 mil [THT]"]
  LED1 = LED - 5mm [color="Red (633nm)" current=0.030A package="5 mm [THT]"]
  LED2 = LEDs [package=led10mm]
  U1 = DC-DC 2-24V Step Up Booster [package=THT]
  U2 = SWITCH-SPST-2 [package=switch-spst-vertical]
  S6 = Taiway 100-SP-X-T1 SPDT Miniature Toggle Switch [part_number=100-SP-X-T1-0-0-B1-M2 package=THT]
  S7 = Taiway 100-SP-X-T1 SPDT Miniature Toggle Switch [part_number=100-SP-X-T1-0-0-B1-M2 package=THT]
  S8 = Taiway 100-SP-X-T1 SPDT Miniature Toggle Switch [part_number=100-SP-X-T1-0-0-B1-M2 package=THT]
  S9 = Taiway 100-SP-X-T1 SPDT Miniature Toggle Switch [part_number=100-SP-X-T1-0-0-B1-M2 package=THT]
  J2 = Piezo Speaker
  Q2 = PNP-Transistor [package="TO92 [THT]"]
  R3 = Resistor [tolerance=±5% power=0.25W resistance=1k package=THT]
  D3 = Rectifier Diode [part_number=1N4001 package="300 mil [THT]"]
  Mod2 = KY-035 Analog Magnetic Hall Sensor [package="Breakout board"]
  R2 = Resistor [tolerance=±5% power=0.25W resistance=1k package=THT]

nets:
  VSS: LCM1602_IIC1.VSS, LCD1.VSS
  VDD: LCM1602_IIC1.VDD, LCD1.VDD
  N1: LCM1602_IIC1.V0, LCD1.V0
  N2: LCM1602_IIC1.RS, LCD1.RS
  N3: LCM1602_IIC1.RW, LCD1.R/W
  N4: LCM1602_IIC1.E, LCD1.E
  N5: LCM1602_IIC1.D0, LCD1.DB0
  N6: LCM1602_IIC1.D1, LCD1.DB1
  N7: LCM1602_IIC1.D2, LCD1.DB2
  N8: LCM1602_IIC1.D3, LCD1.DB3
  N9: LCM1602_IIC1.D4, LCD1.DB4
  N10: LCM1602_IIC1.D5, LCD1.DB5
  N11: LCM1602_IIC1.D6, LCD1.DB6
  N12: LCM1602_IIC1.D7, LCD1.DB7
  N13: LCM1602_IIC1.A, LCD1.LED+
  N14: LCM1602_IIC1.K, LCD1.LED-
  N15: LCM1602_IIC1.GND, Mod1.pin2, Mod1.pin_9, Mod1.pin_25, Mod1.pin_29, J1.GNDBREAK, Q1.E, LED1.cathode, U1.pin2, U1.pin4, S7.L2, S8.L2, Q2.E, Mod2.-
  N16: LCM1602_IIC1.VCC, Mod1.pin_30, U1.pin3, U2.O
  N17: LCM1602_IIC1.SDA, Mod1.pin_12
  N18: LCM1602_IIC1.SCL, Mod1.pin_13
  N19: LCM1602_IIC1.LED_A, S6.COM
  N20: LCM1602_IIC1.LED_B, S6.L1
  N21: Mod1.pin1, Mod1.pin_26, Mod2.Vin
  N22: Mod1.pin5, R1.Pin_1
  N23: Mod1.pin6, S8.L1
  N24: Mod1.pin7, S7.L1
  N25: Mod1.pin8, D3.cathode
  N26: Mod1.pin_14, D2.cathode
  N27: Mod1.pin_15, Mod2.S
  N28: J1.GND, U2.P
  N29: Q1.B, R2.Pin_0
  N30: Q1.C, LED2.C
  N31: R1.Pin_0, LED1.anode
  N32: D2.anode, R2.Pin_1
  N33: LED2.A, U1.pin1, S9.L1
  N34: S9.L2, J2.pin2
  N35: J2.pin1, Q2.C
  N36: Q2.B, R3.Pin_0
  N37: R3.Pin_1, D3.anode

custom parts:
  LCM1602 IIC: I2C-Module to use a 1602 or 2004 LCD on with the wire.h libory Serial LCD Modul
  LEDs: LEDs Standard schematic elements and footprints for 5mm, 3mm, 1206, and 0603 sized LEDs. 5mm - Spark Fun Electronics SKU : COM-00529 (and others)
  DC-DC 2-24V Step Up Booster: Convertisseur DC-DC 2-24V 2A
  KY-035 Analog Magnetic Hall Sensor: KY-035 analog magnetic hall sensor is a module that reacts in the presence of a magnet. It can measure the polarity and relative strength of a magnetic field.
